# Fritzing sketch PCB (saved by Fritzing 0.9.3b)
circuit board: 3.2781cm x 2.53444cm
breadboards: 1

parts:
  TSL2591 = Adafruit TSL2591 [part_number="Adafruit #1980"]
  Raspberry_Pi_1 = Raspberry Pi 3 [part_number=RPI-3-V1.2]
  J1 = female pin header, 4 pins [form="♀ (female)"]

nets:
  VIN: TSL2591.VIN, Raspberry_Pi_1.3v3, J1.pin1
  GND: TSL2591.GND, Raspberry_Pi_1.GND, J1.pin2
  N1: TSL2591.SDA, Raspberry_Pi_1.GPIO2, J1.pin3
  N2: TSL2591.SCL, Raspberry_Pi_1.GPIO3, J1.pin4

notes:
  Husnal
  RVR
  SCL
  SDA
  GND
  Vin

custom parts:
  Adafruit TSL2591: When the future is dazzlingly-bright, this ultra-high-range luminosity sensor will help you measure it. The TSL2591 luminosity sensor is an advanced digital light sensor, ideal for use in a wide range of light situations. Compared to low cost CdS cells, this sensor is more precise, allowing for exact lux calculations and can be configured for different gain/timing ranges to detect light ranges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
